// Logisim project zadanie2.circ as structural Verilog: 1 circuit, main circuit main
module main (
  input  a,
  input  b,
  input  c,
  input  d,
  output A_D,
  output B_D,
  output C_D,
  output D_D,
  output B_K,
  output C_K,
  output D_K,
  output AK
);

  wire nA_2_out, nand_1_out, nand_2_out, nand_3_out, nand_4_out, nand_5_out, nand_6_out, nand_7_out,
       nb_2_out, nb_out, nc_2_out, nc_out, nd_2_out, nd_out, nor_1_out, nor_2_out, nor_3_out, nor_4_out,
       nor_5_out, nor_6_out, nor_7_out;

  // NAND_Gate na has open pins: in0=a, in1=a, out=open
  nor nA_2 (nA_2_out, a, a);
  nand nc (nc_out, c, c);
  nand nb (nb_out, b, b);
  nor nc_2 (nc_2_out, c, c);
  nor nb_2 (nb_2_out, b, b);
  nand nd (nd_out, d, d);
  nor nd_2 (nd_2_out, d, d);
  nand nand_1 (nand_1_out, nd_out, nc_out, a);
  nand nand_2 (nand_2_out, a, b);
  nand nand_3 (nand_3_out, b, nc_out, nd_out);
  nand nand_4 (nand_4_out, nb_out, d);
  nand nand_5 (nand_5_out, c, nb_out);
  nand nand_6 (nand_6_out, c, nd_out);
  nand nand_7 (nand_7_out, nc_out, d);
  nor nor_1 (nor_1_out, c, b, d);
  nor nor_2 (nor_2_out, nd_2_out, nb_2_out);
  nor nor_3 (nor_3_out, nb_2_out, nc_2_out);
  nor nor_4 (nor_4_out, d, c);
  nor nor_5 (nor_5_out, nd_2_out, nc_2_out);
  nand nand_8 (A_D, nand_1_out, nand_2_out);
  nand nand_9 (B_D, nand_3_out, nand_4_out, nand_5_out);
  nor nor_6 (nor_6_out, nd_2_out, b);
  nor nor_7 (nor_7_out, nc_2_out, b);
  nand nand_10 (C_D, nand_6_out, nand_7_out);
  nor nor_8 (B_K, nor_1_out, nor_2_out, nor_3_out);
  nor nor_9 (C_K, nor_4_out, nor_5_out);
  nor nor_10 (AK, nor_6_out, nA_2_out, nor_7_out);

  assign D_D = d;
  assign D_K = d;

  // Notes on the sheet:
  //   !(A!C!D)
  //   !(AB)
  //   !(B!C!D)
  //   !(!BD)
  //   !(!BC)
  //   !(C!D)
  //   !(!CD)
  //   !(D+C+B)
  //   !(D+C)
  //   !(!D+!C)
  //   A
  //   B
  //   C
  //   D
  //   A
  //   !(!D+B)
  //   !(!C+B)
  //   B
  //   !(!B+!D)
  //   !(!B+!C)
  //   C
  //   D
  //   !(!(A!C!D) !(AB))
  //   !(!(B!C!D) !(!BD) !(C!D))
  //   !(!(C!D) !(!CD))
  //   !(!(D+C)+!(!D+!C))
  //   !(!(!D+B)+!(!C+B))
  //   !(!(D+C+B)+!(!B+!D)+!(!B+!C))
endmodule
